// Logisim project sap1.circ as structural Verilog
module main (
  input  in_1,
  input  in_2,
  input  in_3,
  input  [3:0] in_4,
  input  in_5,
  input  [7:0] in_6,
  input  in_7,
  input  in_8,
  output out_9,
  output out_10
);

  wire bcd_to_7_segment_decoder_1_p1, binary_to_bcd_converter_1_p3, binary_to_bcd_converter_1_p4,
       clock_1_out, clock_2_out, clock_3_out, clock_4_out, clock_5_out, clock_6_out, clock_7_out,
       controller_1_ce, controller_1_cp, controller_1_ea, controller_1_ei, controller_1_ep, controller_1_eu,
       controller_1_la, controller_1_lb, controller_1_li, controller_1_lm, controller_1_lo, controller_1_lp,
       controller_1_su;
  wire [3:0] fat_1_mar_addr_out, instructionregister_1_ir_opcode_out, programcounter_1_pc_bus_out;
  wire [7:0] accumulator_1_addsub_in, b_reg_1_b_accum_out, outregister_1_out_reg_out,
       ram16x8_1_temp_ram_12_out;
  wire [7:4] programcounter_1_pc_bus_out_2;
  wire [8:8] undriven;

  Clock clock_1 (.out(clock_1_out));
  Clock clock_2 (.out(clock_2_out));
  Clock clock_3 (.out(clock_3_out));
  programcounter programcounter_1 (
    .C_P(controller_1_cp), .nCLK(clock_1_out), .nCLR(in_2), .E_P(controller_1_ep), .L_P(controller_1_lp),
    .pc_bus_in(programcounter_1_pc_bus_out),
    .pc_bus_out({programcounter_1_pc_bus_out_2, programcounter_1_pc_bus_out}));
  FAT fat_1 (
    .LM(controller_1_lm), .CLK(clock_2_out), .bus_in(programcounter_1_pc_bus_out),
    .mar_addr_out(fat_1_mar_addr_out));
  ram16x8 ram16x8_1 (
    .mar_addr(fat_1_mar_addr_out), .CE(controller_1_ce), .WE(in_5), .data_in({undriven[8], in_6}),
    .clk(in_7), .ram_bus_out({programcounter_1_pc_bus_out_2, programcounter_1_pc_bus_out}),
    .temp_ram_12_out(ram16x8_1_temp_ram_12_out));
  instructionregister instructionregister_1 (
    .L_I(controller_1_li), .CLK(clock_3_out), .CLR(in_8), .E_I(controller_1_ei),
    .ir_bus_in({programcounter_1_pc_bus_out_2, programcounter_1_pc_bus_out}),
    .ir_addr_out(programcounter_1_pc_bus_out), .ir_opcode_out(instructionregister_1_ir_opcode_out));
  Controller controller_1 (
    .clk(clock_4_out), .clr(in_1), .inst_in(instructionregister_1_ir_opcode_out), .Cp(controller_1_cp),
    .Ep(controller_1_ep), .Lm(controller_1_lm), .CE(controller_1_ce), .Li(controller_1_li),
    .Ei(controller_1_ei), .La(controller_1_la), .Ea(controller_1_ea), .Su(controller_1_su),
    .Eu(controller_1_eu), .Lb(controller_1_lb), .Lo(controller_1_lo), .Lp(controller_1_lp), .HLT(out_9));
  Clock clock_4 (.out(clock_4_out));
  Clock clock_5 (.out(clock_5_out));
  Clock clock_6 (.out(clock_6_out));
  Clock clock_7 (.out(clock_7_out));
  accumulator accumulator_1 (
    .L_A(controller_1_la), .CLK(clock_5_out), .E_A(controller_1_ea),
    .acc_bus_in({programcounter_1_pc_bus_out_2, programcounter_1_pc_bus_out}),
    .acc_bus_out({programcounter_1_pc_bus_out_2, programcounter_1_pc_bus_out}),
    .addsub_in(accumulator_1_addsub_in), .Z(out_10));
  test test_1 (
    .A(accumulator_1_addsub_in), .B(b_reg_1_b_accum_out), .S_U(controller_1_su), .E_U(controller_1_eu),
    .hello_hi_bus_out({programcounter_1_pc_bus_out_2, programcounter_1_pc_bus_out}));
  b_reg b_reg_1 (
    .L_B(controller_1_lb), .CLK(clock_6_out),
    .b_bus_in({programcounter_1_pc_bus_out_2, programcounter_1_pc_bus_out}), .b_accum_out(b_reg_1_b_accum_out));
  outregister outregister_1 (
    .L_O(controller_1_lo), .CLK(clock_7_out),
    .out_bus_in({programcounter_1_pc_bus_out_2, programcounter_1_pc_bus_out}),
    .out_reg_out(outregister_1_out_reg_out));
  // BCD_to_7_Segment_decoder bcd_to_7_segment_decoder_1: pin names not known; wires that end beside it: bcd_to_7_segment_decoder_1_p1
  _7_Segment_Display u_7_segment_display_1 ();  // open: g, f, a, b, e, d, c, dp
  // Binary_to_BCD_converter #(.binvalue(8)) binary_to_bcd_converter_1: pin names not known; wires that end beside it: outregister_1_out_reg_out, bcd_to_7_segment_decoder_1_p1, binary_to_bcd_converter_1_p3, binary_to_bcd_converter_1_p4
  // BCD_to_7_Segment_decoder bcd_to_7_segment_decoder_2: pin names not known; wires that end beside it: binary_to_bcd_converter_1_p3
  // BCD_to_7_Segment_decoder bcd_to_7_segment_decoder_3: pin names not known; wires that end beside it: binary_to_bcd_converter_1_p4
  _7_Segment_Display u_7_segment_display_2 ();  // open: g, f, a, b, e, d, c, dp
  _7_Segment_Display u_7_segment_display_3 ();  // open: g, f, a, b, e, d, c, dp
  // Pins of 8 and 9 bits meet at {undriven[8], in_6}
endmodule

// VHDL entity programcounter, as the project stores it:
library IEEE;
use IEEE.std_logic_1164.all;
use IEEE.numeric_std.all;

-- c_p = when active increment on falling edge
-- e_p = when active put program register onto bus
-- nclr = active low clr
-- nclk = active low clk

entity programcounter is -- WORKING
  port (
    C_P        : in std_logic;
    nCLK       : in std_logic;
    nCLR       : in std_logic;
    E_P        : in std_logic; -- will be used on top level implementation
    L_P        : in std_logic;
    pc_bus_in  : in std_logic_vector(3 downto 0);
    pc_bus_out : out std_logic_vector(7 downto 0)
  );
end;

architecture programcounter_rtl of programcounter is
  signal programcounter_reg : unsigned(3 downto 0) := (others => '0');
begin
  process (nCLK)
  begin
    if nCLR = '0' then
      programcounter_reg <= (others => '0');
    elsif falling_edge(nCLK) then
      if L_P = '1' then
  programcounter_reg <= unsigned(pc_bus_in);
elsif C_P = '1' then
  programcounter_reg <= programcounter_reg + 1;
end if;
    end if;
  end process;
  pc_bus_out <= "0000" & std_logic_vector(programcounter_reg) when E_P = '1' else
    (others => 'Z');
end architecture;

// VHDL entity accumulator, as the project stores it:
library IEEE;
use IEEE.std_logic_1164.all;
use IEEE.numeric_std.all;
--nL_A = active low loading into accumulator
--e_a = active high loading from accumulator onto bus
-- CLK = active high clock

entity accumulator is --WORKING
  port (
    L_A        : in std_logic;
    CLK         : in std_logic;
    E_A         : in std_logic;
    acc_bus_in  : in std_logic_vector(7 downto 0);
    acc_bus_out : out std_logic_vector(7 downto 0);
    addsub_in   : out std_logic_vector(7 downto 0);
    Z :out std_logic 

  );
end;
architecture accumulator_rtl of accumulator is
  signal accumulator_reg : std_logic_vector(7 downto 0) := (others => '0');
  signal Z_reg : std_logic := '0';
begin
  process (CLK)
  begin
    if rising_edge(CLK) then
      if L_A = '1' then
        accumulator_reg <= acc_bus_in;

        if acc_bus_in = "00000000" then
        	Z_reg <= '1';
        else
         Z_reg <= '0';
        end if;
      end if;
    end if;
  end process;

  acc_bus_out <= accumulator_reg when E_A = '1' else
    (others => 'Z');

  addsub_in <= accumulator_reg;
end architecture;

// VHDL entity b_reg, as the project stores it:
library IEEE;
use IEEE.std_logic_1164.all;
use IEEE.numeric_std.all;

entity b_reg is --WORKING
  port (
    L_B        : in std_logic;
    CLK         : in std_logic;
    b_bus_in    : in std_logic_vector(7 downto 0);
    b_accum_out : out std_logic_vector(7 downto 0)

  );
end;

architecture b_rtl of b_reg is
  signal b_reg : std_logic_vector(7 downto 0) := (others => '0');
begin
  process (CLK)
  begin
    if rising_edge(CLK) then
      if L_B = '1' then
        b_reg <= b_bus_in;
      end if;
    end if;
  end process;

  b_accum_out <= b_reg;
end architecture;

// VHDL entity ram16x8, as the project stores it:
library IEEE;
use IEEE.std_logic_1164.all;
use IEEE.numeric_std.all;

entity ram16x8 is
  port (
    mar_addr        : in std_logic_vector(3 downto 0);
    CE              : in std_logic; -- active high
    ram_bus_out     : out std_logic_vector(7 downto 0);
    WE              : in std_logic;
    data_in         : in std_logic_vector(8 downto 0);
    clk             : in std_logic;
    temp_ram_12_out : out std_logic_vector (7 downto 0)
  );
end;

architecture rtl_ram of ram16x8 is
  type ram_type is array (0 to 15) of std_logic_vector(7 downto 0);
  signal ram : ram_type := (
  0  => "00001001", -- LDA @9
  1  => "00011100", -- ADD @12
  2  => "11101111", -- OUT
  3  => "00000000", -- JMP @1
  4  => "01100001", -- HLT (unused)
  5  => "00000000",
  6  => "00000000",
  7  => "00000000",
  8  => "00000000",
  9  => "00000001",
  10 => "00000001",
  11 => "00000001",
  12 => "00000001",
  13 => "00000000",
  14 => "00000000",
  15 => "00000000"
  );
begin
  process (clk)
  begin
    if clk = '1' then
      if CE = '1' and WE = '1' then
        ram(to_integer(unsigned(mar_addr))) <= data_in;
      end if;
    end if;
  end process;
  temp_ram_12_out <= ram(12);
  ram_bus_out     <= ram(to_integer(unsigned(mar_addr))) when CE = '1' else
    (others => 'Z');
end architecture;

// VHDL entity test, as the project stores it:
library IEEE;
use IEEE.std_logic_1164.all;
use IEEE.numeric_std.all;

entity test is
  port (
    A                : in std_logic_vector(7 downto 0);
    B                : in std_logic_vector(7 downto 0);
    S_U              : in std_logic; -- 0 = ADD, 1 = SUB
    E_U              : in std_logic; -- enable to bus
    hello_hi_bus_out : out std_logic_vector(7 downto 0)
  );
end;

architecture hello_hi_rtl of test is

  signal result : std_logic_vector(7 downto 0);
begin

  process (A, B, S_U)
  begin
    if S_U = '0' then
      result <= std_logic_vector(unsigned(A) + unsigned(B));
    else
      result <= std_logic_vector(unsigned(A) - unsigned(B));
    end if;
  end process;

  hello_hi_bus_out <= result when E_U = '1' else
    (others => 'Z');

end;

// VHDL entity mar, as the project stores it:
library IEEE;
use IEEE.std_logic_1164.all;
use IEEE.numeric_std.all;

-- nLM = active low allowing input from bus into mar
-- bus_in = bus input
-- mar_addr_out = address output to ram

entity mar is
  port (
    LM           : in std_logic;
    CLK          : in std_logic;
    bus_in       : in std_logic_vector(3 downto 0);
    mar_addr_out : out std_logic_vector(3 downto 0)
  );
end;

architecture mar_rtl of mar is
  signal mar_reg : std_logic_vector(3 downto 0) := (others => '0');
begin
  process (CLK)
  begin
    if rising_edge(CLK) then
      if LM = '1' then
        mar_reg <= bus_in; -- only lower 4 bits
      end if;
    end if;
  end process;

  mar_addr_out <= mar_reg;
end architecture;

// VHDL entity instructionregister, as the project stores it:
library IEEE;
use IEEE.std_logic_1164.all;
use IEEE.numeric_std.all;

entity instructionregister is
  port (
    L_I          : in std_logic;
    CLK           : in std_logic;
    CLR           : in std_logic;
    E_I          : in std_logic;
    ir_bus_in     : in std_logic_vector (7 downto 0);
    ir_addr_out   : out std_logic_vector (3 downto 0);
    ir_opcode_out : out std_logic_vector (3 downto 0)
  );
end;

architecture instructionregister_rtl of instructionregister is
  signal ir_reg : std_logic_vector (7 downto 0) := (others => '0');
begin
  process (clk, CLR)
  begin
    if CLR = '0' then
      ir_reg <= (others => '0');
    elsif falling_edge(clk) then
      if L_I = '1' then
        ir_reg <= ir_bus_in;
      end if;
    end if;
  end process;
  ir_opcode_out <= ir_reg(7 downto 4);
  ir_addr_out   <= ir_reg (3 downto 0) when E_I = '1' else
    (others => 'Z');
end architecture;

// VHDL entity outregister, as the project stores it:
library IEEE;
use IEEE.std_logic_1164.all;
use IEEE.numeric_std.all;

entity outregister is
  port (
    L_O        : in std_logic;
    CLK         : in std_logic;
    out_bus_in  : in std_logic_vector (7 downto 0);
    out_reg_out : out std_logic_vector (7 downto 0)
  );
end;

architecture outregister_rtl of outregister is
  signal out_reg : std_logic_vector (7 downto 0) := (others => '0');
begin
  process (clk)
  begin
    if rising_edge(clk) then
      if L_O = '1' then
        out_reg <= out_bus_in;
      end if;
    end if;
  end process;
  out_reg_out <= out_reg;
end architecture;

// VHDL entity Controller, as the project stores it:
library IEEE;
use IEEE.STD_LOGIC_1164.all;
use IEEE.STD_LOGIC_ARITH.all;
use IEEE.STD_LOGIC_UNSIGNED.all;

entity Controller is
  port (
    clk     : in std_logic;
    clr     : in std_logic;
    inst_in : in std_logic_vector (3 downto 0);
    Cp      : out std_logic;
    Ep      : out std_logic;
    Lm      : out std_logic;
    CE      : out std_logic;
    Li      : out std_logic;
    Ei      : out std_logic;
    La      : out std_logic;
    Ea      : out std_logic;
    Su      : out std_logic;
    Eu      : out std_logic;
    Lb      : out std_logic;
    Lo      : out std_logic;
    Lp      : out std_logic;
    HLT     : out std_logic);
end Controller;

architecture Behavioral of Controller is

  type state is (idle, t0, t1, t2, t3, t4, t5);
  signal pr_state, nx_state : state                          := t0;
  signal control_signal     : std_logic_vector (12 downto 0) := (others => '0');
  signal HLT_sig            : std_logic                      := '1';

begin

  -- This process if for updating current state.
  process (clk, clr)
  begin
    if clr = '0' then
      pr_state <= idle;
    elsif rising_edge(clk) then
      pr_state <= nx_state;
    end if;
  end process;
  -- This process does the actual transition logic and operations.
  process (pr_state)
  begin
    case pr_state is
      when idle =>
        --Do nothing
        control_signal <= "0000000000000";
        HLT_sig        <= '1';
        nx_state       <= t0;

      when t0 =>
        --Enable PC (Ep = 1), Load into MAR (Lm = 1)
        control_signal <= "0011000000000";
        nx_state       <= t1;

      when t1 =>
        --Increment PC (Cp = 1)
        control_signal <= "0100000000000";
        nx_state       <= t2;

      when t2 =>
        --Enable memory (CE = 1), Load into IR (Li = 1)
        control_signal <= "0000110000000";
        nx_state       <= t3;

      when t3 =>
        --OUT
        if inst_in = "1110" then
          --Enable AC, Load into OUT
          control_signal <= "0000000010001";
          --HALT
        elsif inst_in = "1111" then
          control_signal <= "0000000000000";
          HLT_sig        <= '0';
          --Other instructions
        elsif inst_in = "0110" then
  control_signal <= "1000001000000"; -- Ei only
        else
          control_signal <= "0001001000000";
        end if;
        nx_state <= t4;

      when t4 =>
        --LDA
        if inst_in = "0000" then
          --Enable memory, Load into AC
          control_signal <= "0000100100000";
          --ADD
        elsif inst_in = "0001" then
          --Enable memory, Load into B
          control_signal <= "0000100000010";
          --SUB
        elsif inst_in = "0010" then
          --Enable memory, Load into B
          control_signal <= "0000100000010";
          --Other instructions
        else
          control_signal <= "0000000000000";
        end if;
        nx_state <= t5;

      when t5 =>
        --ADD
        if inst_in = "0001" then
          --Enable ALU, Load into AC, Su = 0 for ADD
          control_signal <= "0000000100100";
          --SUB
        elsif inst_in = "0010" then
          --Enable ALU, Load into AC, Su = 1 for SUB
          control_signal <= "0000000101100";
          --Other instructions
        else
          control_signal <= "0000000000000";
        end if;
        nx_state <= t0;

    end case;
  end process;

  --Move control signal to output
  Lp  <= control_signal(12);
  Cp  <= control_signal(11);
  Ep  <= control_signal(10);
  Lm  <= control_signal(9);
  CE  <= control_signal(8);
  Li  <= control_signal(7);
  Ei  <= control_signal(6);
  La  <= control_signal(5);
  Ea  <= control_signal(4);
  Su  <= control_signal(3);
  Eu  <= control_signal(2);
  Lb  <= control_signal(1);
  Lo  <= control_signal(0);
  HLT <= HLT_sig;

end Behavioral;

// VHDL entity FAT, as the project stores it:
library IEEE;
use IEEE.std_logic_1164.all;
use IEEE.numeric_std.all;

-- nLM = active low allowing input from bus into mar
-- bus_in = bus input
-- mar_addr_out = address output to ram

entity FAT is
  port (
    LM           : in std_logic;
    CLK          : in std_logic;
    bus_in       : in std_logic_vector(3 downto 0);
    mar_addr_out : out std_logic_vector(3 downto 0)
  );
end;

architecture mar_rtl of FAT is
  signal mar_reg : std_logic_vector(3 downto 0) := (others => '0');
begin
  process (CLK)
  begin
    if rising_edge(CLK) then
      if LM = '1' then
        mar_reg <= bus_in; -- only lower 4 bits
      end if;
    end if;
  end process;

  mar_addr_out <= mar_reg;
end architecture;
